// Logisim project 4_Gate_and_it_value.circ as structural Verilog: 1 circuit, main circuit main
module main (
  input  A,
  input  A_2,
  input  A_3,
  input  A_4,
  input  B,
  input  B_2,
  input  B_3,
  input  B_4,
  output Output,
  output Output_2,
  output Output_3,
  output Output_4
);

  and and_1 (Output, A, B);
  or or_1 (Output_2, A_2, B_2);
  nand nand_1 (Output_3, A_3, B_3);
  nor nor_1 (Output_4, A_4, B_4);

  // Notes on the sheet:
  //     A   |  B  |  OutPut 
  //     0   |  0   |      0      
  //     1   |  0   |      0      
  //     0   |  1   |      0      
  //     1   |  1   |      1      
  //     A   |  B  |  OutPut 
  //     0   |  0   |      0      
  //     1   |  0   |      1      
  //     0   |  1   |      1      
  //     1   |  1   |      1      
  //     A   |  B  |  OutPut 
  //     0   |  0   |      1      
  //     1   |  0   |      1      
  //     0   |  1   |      1      
  //     1   |  1   |      0      
  //     A   |  B  |  OutPut 
  //     0   |  0   |      1      
  //     1   |  0   |      0      
  //     0   |  1   |      0      
  //     1   |  1   |      0      
endmodule
