// Logisim project AssignmentQ2E.circ as structural Verilog: 1 circuit, main circuit main
module main (
  input  W,
  input  X,
  input  Y,
  input  Z,
  output out_5
);

  wire nor_1_out, nor_2_out, nor_3_out, nor_4_out, nor_5_out, nor_6_out;

  nor nor_1 (nor_1_out, Z, Z);
  nor nor_2 (nor_2_out, W, W);
  nor nor_3 (nor_3_out, nor_1_out, Y);
  nor nor_4 (nor_4_out, W, Y);
  nor nor_5 (nor_5_out, nor_1_out, nor_2_out, X);
  nor nor_6 (nor_6_out, nor_3_out, nor_4_out, nor_5_out);
  nor nor_7 (out_5, nor_6_out, nor_6_out);

  // Notes on the sheet:
  //   W
  //   Y
  //   W'
  //   X
  //   Z'
  //   Y
endmodule
