// Logisim project AssignmentQ2c.circ as structural Verilog: 1 circuit, main circuit main
module main (
  input  W,
  input  X,
  input  Y,
  input  Z,
  output F
);

  wire and_1_out, and_2_out, and_3_out, and_4_out, not_1_out, not_2_out, not_3_out, or_1_out;

  not not_1 (not_1_out, W);
  not not_2 (not_2_out, X);
  not not_3 (not_3_out, Y);
  and and_1 (and_1_out, not_1_out, not_3_out);
  and and_2 (and_2_out, not_3_out, Z);
  and and_3 (and_3_out, W, not_2_out);
  or or_1 (or_1_out, and_1_out, and_2_out);
  and and_4 (and_4_out, and_3_out, Z);
  or or_2 (F, or_1_out, and_4_out);

  // Notes on the sheet:
  //   2211950642
  //   Answer to the Q no 2 (c)
  //   MD Rokib Hasan Oli
  //   W'
  //   Y'
  //   Y'
  //   Z
  //   W
  //   X'
  //   W'.Y'
  //   Y'.Z
  //   W.X'
  //   Z
  //   W'.Y'+Y'.Z
  //   W.X'.Z
  //   = W'.Y'+Y'.Z+W.X'.Z
endmodule
