// Logisim project AssignmentQ2d.circ as structural Verilog: 1 circuit, main circuit main
module main (
  input  W,
  input  X,
  input  Y,
  input  Z,
  output out_5
);

  wire nand_1_out, nand_2_out, nand_3_out, nand_4_out, nand_5_out, nand_6_out;

  nand nand_1 (nand_1_out, W, W);
  nand nand_2 (nand_2_out, X, X);
  nand nand_3 (nand_3_out, Y, Y);
  nand nand_4 (nand_4_out, nand_1_out, nand_3_out);
  nand nand_5 (nand_5_out, nand_3_out, Z);
  nand nand_6 (nand_6_out, nand_2_out, W, Z);
  nand nand_7 (out_5, nand_4_out, nand_5_out, nand_6_out);

  // Notes on the sheet:
  //   MD Rokib Hasan Oli
  //   2211950642
  //   W'
  //   X'
  //   Y'
  //   (W'.Y')'
  //   (Y'.Z)'
  //   (W.X'.Z)'
  //   F=((W'.Y')'.(Y'.Z)'.(W.X'.Z)')'
endmodule
