// Logisim project Assignment_2_Q1_a.circ as structural Verilog: 1 circuit, main circuit main
module main (
  input  X,
  output out_2,
  output out_3
);

  wire and_1_out, and_2_out, clock_1_out, j_k_ff_1_qn, not_1_out, or_1_out, or_2_out;

  Clock clock_1 (.out(clock_1_out));
  not not_1 (not_1_out, X);
  J_K_Flip_Flop j_k_ff_1 (
    .J(not_1_out), .K(out_3), .clk(clock_1_out), .Q(out_2), .Qn(j_k_ff_1_qn));  // open: preset, reset
  and and_1 (and_1_out, not_1_out, j_k_ff_1_qn);
  and and_2 (and_2_out, out_2, X);
  or or_1 (or_1_out, and_1_out, and_2_out);
  or or_2 (or_2_out, X, j_k_ff_1_qn);
  J_K_Flip_Flop j_k_ff_2 (.J(or_2_out), .K(or_1_out), .clk(clock_1_out), .Q(out_3));  // open: Qn, preset, reset

  // Notes on the sheet:
  //   MD Rokib Hasan Oli 2211950642
  //   ( A )
  //   A
  //   X'
  //   B
  //   A'+X
  //   A'X'+AX
  //   B
endmodule
