// Logisim project Assignment_2_Q1_b.circ as structural Verilog: 1 circuit, main circuit main
module main (
  input  X,
  output out_2,
  output out_3
);

  wire and_1_out, and_2_out, and_3_out, and_4_out, clock_1_out, j_k_ff_1_qn, j_k_ff_2_qn, not_1_out,
       or_1_out, or_2_out;

  Clock clock_1 (.out(clock_1_out));
  not not_1 (not_1_out, X);
  and and_1 (and_1_out, not_1_out, j_k_ff_1_qn);
  and and_2 (and_2_out, out_3, out_2);
  or or_1 (or_1_out, and_2_out, and_1_out);
  J_K_Flip_Flop j_k_ff_1 (
    .J(or_1_out), .K(or_1_out), .clk(clock_1_out), .Q(out_2), .Qn(j_k_ff_1_qn));  // open: preset, reset
  or or_2 (or_2_out, and_4_out, and_1_out, and_3_out);
  and and_3 (and_3_out, out_2, X);
  J_K_Flip_Flop j_k_ff_2 (
    .J(or_2_out), .K(or_2_out), .clk(clock_1_out), .Q(out_3), .Qn(j_k_ff_2_qn));  // open: preset, reset
  and and_4 (and_4_out, j_k_ff_2_qn, X);

  // Notes on the sheet:
  //   MD Rokib Hasan Oli 2211950642
  //   ( B )
  //   A'X'+AB
  //   A
  //   A'X'+AX+B'X
  //   B
endmodule
