// Logisim project Assignment_2_Q1_c.circ as structural Verilog: 1 circuit, main circuit main
module main (
  input  X,
  output out_2,
  output out_3
);

  wire and_1_out, and_2_out, and_3_out, and_4_out, and_5_out, and_6_out, clock_1_out, j_k_ff_1_qn,
       j_k_ff_2_qn, not_1_out, not_2_out, not_3_out, or_1_out, or_2_out;

  Clock clock_1 (.out(clock_1_out));
  not not_1 (not_1_out, X);
  and and_1 (and_1_out, X, out_2);
  and and_2 (and_2_out, not_1_out, j_k_ff_1_qn);
  and and_3 (and_3_out, out_2, j_k_ff_2_qn);
  or or_1 (or_1_out, and_2_out, and_3_out);
  and and_4 (and_4_out, X, j_k_ff_2_qn);
  J_K_Flip_Flop j_k_ff_1 (
    .J(or_1_out), .K(not_2_out), .clk(clock_1_out), .Q(out_2), .Qn(j_k_ff_1_qn));  // open: preset, reset
  not not_2 (not_2_out, or_1_out);
  and and_5 (and_5_out, out_2, not_1_out, out_3);
  not not_3 (not_3_out, or_2_out);
  and and_6 (and_6_out, j_k_ff_1_qn, j_k_ff_2_qn);
  J_K_Flip_Flop j_k_ff_2 (
    .J(or_2_out), .K(not_3_out), .clk(clock_1_out), .Q(out_3), .Qn(j_k_ff_2_qn));  // open: preset, reset
  or or_2 (or_2_out, and_1_out, and_4_out, and_6_out, and_5_out);

  // Notes on the sheet:
  //   MD Rokib Hasan Oli 2211950642
  //   ( C )
  //   A'X'+AB'
  //   A
  //   ABX'+A'B'+A'X+B'X
  //   B
endmodule
