// Logisim project Assignment_2_Q2.circ as structural Verilog: 1 circuit, main circuit main
module main (
  input  D0,
  output T1,
  output T2,
  output T3,
  output T4
);

  wire clock_1_out;

  Clock clock_1 (.out(clock_1_out));
  _7474 u_7474_1 (
    .pin2(D0), .pin3(clock_1_out), .pin5(T1), .pin12(T1), .pin11(clock_1_out), .pin9(T2));  // open: pin1, pin4, pin6, pin13, pin10, pin8
  _7474 u_7474_2 (
    .pin2(T2), .pin3(clock_1_out), .pin5(T3), .pin12(T3), .pin11(clock_1_out), .pin9(T4));  // open: pin1, pin4, pin6, pin13, pin10, pin8

  // Notes on the sheet:
  //   left to right shift Register
  //   MD. Rokib Hasan Oli
  //   2211950642
  //   Q. NO -> 2
endmodule
