// Logisim project D2.circ as structural Verilog: 1 circuit, main circuit main
module main (
  input  X,
  output out_2,
  output out_3
);

  wire and_1_out, and_2_out, clock_1_out, j_k_ff_1_qn, j_k_ff_2_qn, not_1_out, or_1_out;

  Clock clock_1 (.out(clock_1_out));
  not not_1 (not_1_out, X);
  J_K_Flip_Flop j_k_ff_1 (.J(X), .clk(clock_1_out), .K(X), .Q(out_2), .Qn(j_k_ff_1_qn));  // open: preset, reset
  J_K_Flip_Flop j_k_ff_2 (
    .J(or_1_out), .clk(clock_1_out), .K(or_1_out), .Q(out_3), .Qn(j_k_ff_2_qn));  // open: preset, reset
  and and_1 (and_1_out, j_k_ff_1_qn, j_k_ff_2_qn, not_1_out);
  and and_2 (and_2_out, X, out_3);
  or or_1 (or_1_out, and_1_out, and_2_out);

  // Notes on the sheet:
  //   Group 06
  //   M Istiaque Ahmmed 2021015642
  //   Ta
  //   a
  //   a'
  //   b
  //   Tb
  //   b'
endmodule
