// Logisim project J1.circ as structural Verilog: 1 circuit, main circuit main
module main (
  input  X,
  output out_2,
  output out_3
);

  wire and_1_out, and_2_out, and_3_out, clock_1_out, j_k_ff_1_qn, not_1_out, not_2_out, not_3_out, not_4_out,
       or_1_out;

  Clock clock_1 (.out(clock_1_out));
  not not_1 (not_1_out, X);
  and and_1 (and_1_out, out_2, not_1_out);
  and and_2 (and_2_out, X, j_k_ff_1_qn);
  not not_2 (not_2_out, or_1_out);
  or or_1 (or_1_out, and_1_out, and_2_out);
  J_K_Flip_Flop j_k_ff_1 (
    .J(or_1_out), .clk(clock_1_out), .K(not_2_out), .Q(out_2), .Qn(j_k_ff_1_qn));  // open: preset, reset
  not not_3 (not_3_out, and_3_out);
  J_K_Flip_Flop j_k_ff_2 (.J(and_3_out), .clk(clock_1_out), .K(not_3_out), .Q(out_3));  // open: Qn, preset, reset
  not not_4 (not_4_out, X);
  and and_3 (and_3_out, j_k_ff_1_qn, not_4_out);

  // Notes on the sheet:
  //   Group 06
  //   M Istiaque Ahmmed 2021015642
  //   Da
  //   A
  //   Db
  //   B
  //   A'
  //   X'
endmodule
