// Logisim project Lab_1.circ as structural Verilog: 1 circuit, main circuit main
module main (
  input  in_1,
  input  in_2,
  input  in_3,
  input  in_4,
  input  in_5,
  input  in_6,
  input  in_7,
  input  in_8,
  input  in_9,
  input  in_10,
  input  in_11,
  input  in_12,
  input  in_13,
  input  in_14,
  input  in_15,
  input  in_16,
  input  in_17,
  input  A,
  input  B,
  input  C,
  output out_21,
  output out_22,
  output out_23,
  output out_24,
  output out_25,
  output out_26,
  output out_27,
  output out_28,
  output F___I1___I2___I3
);

  wire and_2_out, and_4_out, and_5_out, and_6_out, not_2_out, not_3_out, or_2_out, or_3_out;

  and and_1 (out_21, in_1, in_7);
  and and_2 (and_2_out, in_12, in_14);
  or or_1 (out_22, in_2, in_8);
  and and_3 (out_27, and_2_out, in_16);
  not not_1 (out_23, in_6);
  not not_2 (not_2_out, A);
  not not_3 (not_3_out, B);
  and and_4 (and_4_out, not_2_out, C);
  and and_5 (and_5_out, A, not_3_out);
  and and_6 (and_6_out, B, C);
  nand nand_1 (out_24, in_3, in_9);
  or or_2 (or_2_out, and_4_out, and_5_out);
  or or_3 (or_3_out, in_13, in_15);
  or or_4 (out_28, or_3_out, in_17);
  or or_5 (F___I1___I2___I3, or_2_out, and_6_out);
  nor nor_1 (out_25, in_4, in_10);
  xor xor_1 (out_26, in_5, in_11);

  // Notes on the sheet:
  //   Input 𝐴𝐵𝐶 = 010
  //   I1 = A'.C
  //   I2 = A.B'
  //   I3 = B.C
  //   CSE 231L Sec: 8
  //   Group Number: 6
  //   MD Rokib Hasan Oli   2211950642
endmodule
