// Logisim project Lab_3.circ as structural Verilog: 1 circuit, main circuit main
module main (
  input  A,
  input  B,
  input  C,
  input  A_2,
  input  B_2,
  input  C_2,
  input  A_3,
  input  B_3,
  input  C_3,
  input  A_4,
  input  B_4,
  input  C_4,
  output AC,
  output out_14,
  output B_C_prime,
  output AC_2,
  output out_17,
  output out_18,
  output AC_3,
  output out_20,
  output out_21,
  output out_22
);

  wire nand_1_out, nand_2_out, nand_3_out, nand_6_out, nand_7_out, nor_1_out, nor_2_out, nor_3_out,
       nor_4_out, nor_5_out, nor_6_out, nor_9_out, nor_10_out, nor_11_out, nor_12_out, nor_13_out, not_1_out;

  not not_1 (not_1_out, C);
  nor nor_1 (nor_1_out, C_3, C_3);
  and and_1 (AC, A, C);
  and and_2 (B_C_prime, B, not_1_out);
  nand nand_1 (nand_1_out, A_2, C_2);
  nand nand_2 (nand_2_out, C_2, C_2);
  nor nor_2 (nor_2_out, A_3, C_3);
  nor nor_3 (nor_3_out, A_4, A_4);
  nor nor_4 (nor_4_out, B_4, B_4);
  nor nor_5 (nor_5_out, C_4, C_4);
  nand nand_3 (nand_3_out, B_2, nand_2_out);
  nor nor_6 (nor_6_out, B_3, nor_1_out);
  or or_1 (out_14, AC, B_C_prime);
  nand nand_4 (AC_2, nand_1_out, nand_1_out);
  nor nor_7 (AC_3, nor_2_out, nor_2_out);
  nand nand_5 (out_18, nand_3_out, nand_3_out);
  nor nor_8 (out_21, nor_6_out, nor_6_out);
  nor nor_9 (nor_9_out, nor_3_out, nor_5_out);
  nor nor_10 (nor_10_out, nor_4_out, C_4);
  nand nand_6 (nand_6_out, AC_2, AC_2);
  nand nand_7 (nand_7_out, out_18, out_18);
  nor nor_11 (nor_11_out, AC_3, AC_3);
  nor nor_12 (nor_12_out, out_21, out_21);
  nor nor_13 (nor_13_out, nor_9_out, nor_10_out);
  nor nor_14 (out_20, nor_11_out, nor_12_out);
  nand nand_8 (out_17, nand_6_out, nand_7_out);
  nor nor_15 (out_22, nor_13_out, nor_13_out);

  // Notes on the sheet:
  //   B C'
  //   B C'
endmodule
