// Logisim project Lab_6.circ as structural Verilog: 1 circuit, main circuit main
module main (
  input  D,
  input  D_NOT,
  input  C_NOT,
  input  B_NOT,
  output e,
  output a,
  output f,
  output b,
  output c,
  output g,
  output d_2
);

  wire and_1_out, and_2_out, and_3_out, and_4_out, and_5_out, and_6_out, and_7_out, and_8_out, and_9_out,
       and_10_out, and_11_out, and_12_out, and_13_out, and_14_out, and_15_out, and_16_out, and_17_out,
       and_18_out, not_2_out, not_3_out, not_4_out, or_4_out, or_5_out, or_6_out, or_7_out, or_8_out,
       or_9_out, or_11_out, or_12_out, or_13_out, or_14_out;

  or or_1 (f, or_4_out, or_5_out);
  or or_2 (g, or_6_out, or_7_out);
  or or_3 (e, and_1_out, and_2_out);
  or or_4 (or_4_out, and_3_out, and_4_out);
  or or_5 (or_5_out, and_5_out, D);
  or or_6 (or_6_out, D, and_6_out);
  or or_7 (or_7_out, and_7_out, and_8_out);
  and and_1 (and_1_out, not_2_out, not_4_out);
  and and_2 (and_2_out, C_NOT, not_4_out);
  and and_3 (and_3_out, not_3_out, not_4_out);
  and and_4 (and_4_out, not_4_out, D_NOT);
  and and_5 (and_5_out, D_NOT, not_3_out);
  and and_6 (and_6_out, D_NOT, not_3_out);
  and and_7 (and_7_out, not_2_out, C_NOT);
  and and_8 (and_8_out, C_NOT, not_4_out);
  // NOT_Gate not_1 has open pins: in=D, out=open
  _7_Segment_Display u_7_segment_display_1 (.g(g), .f(f), .a(a), .b(b), .e(e), .d(d_2), .c(c));  // open: dp
  not not_2 (not_2_out, D_NOT);
  not not_3 (not_3_out, C_NOT);
  not not_4 (not_4_out, B_NOT);
  and and_9 (and_9_out, not_2_out, not_4_out);
  and and_10 (and_10_out, D_NOT, B_NOT);
  and and_11 (and_11_out, not_2_out, C_NOT);
  and and_12 (and_12_out, C_NOT, B_NOT);
  and and_13 (and_13_out, not_3_out, not_4_out);
  or or_8 (or_8_out, not_3_out, D_NOT);
  and and_14 (and_14_out, not_2_out, not_4_out);
  and and_15 (and_15_out, not_2_out, C_NOT);
  and and_16 (and_16_out, C_NOT, not_4_out);
  and and_17 (and_17_out, not_3_out, B_NOT);
  or or_9 (or_9_out, and_12_out, and_13_out);
  or or_10 (c, or_8_out, B_NOT);
  or or_11 (or_11_out, and_14_out, and_15_out);
  and and_18 (and_18_out, and_17_out, D_NOT);
  or or_12 (or_12_out, and_9_out, and_10_out);
  or or_13 (or_13_out, and_11_out, D);
  or or_14 (or_14_out, and_16_out, and_18_out);
  or or_15 (b, or_9_out, not_2_out);
  or or_16 (d_2, or_11_out, or_14_out);
  or or_17 (a, or_12_out, or_13_out);

  // Notes on the sheet:
  //   CSE 231L Sec: 8
  //   Group Number: 6
  //   F=C'A'+BA'
  //   F=D+B'A'+CA'+CB'
  //   F=CB'+D+C'B+BA'
  //   MD Rokib Hasan Oli   2211950642
  //   C'A'
  //   BA'
  //   B'A'
  //   CA'
  //   CB'
  //   CB'
  //   C'B
  //   BA'
  //   C
  //   B
  //   A
  //   A NOT
  //   C'A'
  //   CA
  //   C'B
  //   BA
  //   B'A'
  //   C'A'
  //   C'B
  //   BA'
  //   B'A
  //   C'
  //   CB'A
  //   F=B'+C+A
  //   F=D+C'A'+CA+C'B
  //   F=BA+B'A'+C'
  //   F=C'A'+CB'A+C'B+BA'
endmodule
