// Logisim project Lab_8_1.circ as structural Verilog: 1 circuit, main circuit main
module main (
  input  in_1,
  input  in_2,
  output Q,
  output NOT_Q,
  output out_5,
  output out_6
);

  wire and_1_out, and_2_out, clock_1_out;

  Clock clock_1 (.out(clock_1_out));
  J_K_Flip_Flop j_k_ff_1 (.J(in_1), .K(in_2), .clk(clock_1_out), .Q(Q), .Qn(NOT_Q));  // open: preset, reset
  and and_1 (and_1_out, out_5, in_2, clock_1_out);
  and and_2 (and_2_out, clock_1_out, in_1, out_6);
  nor nor_1 (out_5, and_1_out, out_6);
  nor nor_2 (out_6, out_5, and_2_out);

  // Notes on the sheet:
  //   CSE 231L Sec: 8
  //   MD. Rokib Hasan Oli
  //   2211950642
  //   Group Number: 6
endmodule
