// Logisim project Lab_8_2.circ as structural Verilog: 1 circuit, main circuit main
module main (
  input  J,
  input  K,
  input  D0,
  input  T,
  input  D,
  output Q,
  output Q_NOT,
  output out_8,
  output out_9,
  output out_10,
  output out_11,
  output out_12,
  output out_13
);

  wire clock_1_out, clock_2_out, clock_3_out, clock_4_out, not_1_out;

  Clock clock_1 (.out(clock_1_out));
  J_K_Flip_Flop j_k_ff_1 (.J(T), .K(T), .clk(clock_1_out), .Q(out_8));  // open: Qn, preset, reset
  J_K_Flip_Flop j_k_ff_2 (.J(J), .K(K), .clk(clock_2_out), .Q(Q), .Qn(Q_NOT));  // open: preset, reset
  Clock clock_2 (.out(clock_2_out));
  Clock clock_3 (.out(clock_3_out));
  J_K_Flip_Flop j_k_ff_3 (.J(D), .K(not_1_out), .clk(clock_3_out), .Q(out_9));  // open: Qn, preset, reset
  not not_1 (not_1_out, D);
  Clock clock_4 (.out(clock_4_out));
  _7474 u_7474_1 (
    .pin2(D0), .pin3(clock_4_out), .pin5(out_10), .pin12(out_10), .pin11(clock_4_out), .pin9(out_11));  // open: pin1, pin4, pin6, pin13, pin10, pin8
  _7474 u_7474_2 (
    .pin2(out_11), .pin3(clock_4_out), .pin5(out_12), .pin12(out_12), .pin11(clock_4_out), .pin9(out_13));  // open: pin1, pin4, pin6, pin13, pin10, pin8

  // Notes on the sheet:
  //   T Flip-flop using J-K Flip-flop
  //   J-K Flip-flop
  //   D Flip-flop using J-K Flip-flop
  //   Register
  //   CSE 231L Sec: 8
  //   MD. Rokib Hasan Oli
  //   2211950642
  //   Group Number: 6
endmodule
