// Logisim project Project.circ as structural Verilog: 1 circuit, main circuit main
module main (
  input  C,
  input  C_NOT,
  input  B_NOT,
  output a,
  output b,
  output c_2,
  output d,
  output e,
  output f,
  output g
);

  wire and_1_out, and_2_out, and_3_out, and_4_out, and_5_out, and_6_out, and_7_out, and_8_out, and_9_out,
       and_10_out, not_1_out, not_3_out, or_3_out;

  _7_Segment_Display u_7_segment_display_1 (.g(g), .f(f), .a(a), .b(b), .e(e), .d(d), .c(c_2));  // open: dp
  not not_1 (not_1_out, C);
  not not_2 (g, C_NOT);
  not not_3 (not_3_out, B_NOT);
  and and_1 (and_1_out, not_3_out, C);
  and and_2 (and_2_out, not_1_out, C_NOT);
  and and_3 (and_3_out, C, not_3_out);
  and and_4 (and_4_out, C, g);
  and and_5 (and_5_out, not_3_out, C);
  and and_6 (and_6_out, not_3_out, C_NOT);
  and and_7 (and_7_out, not_1_out, g);
  and and_8 (and_8_out, not_3_out, C);
  and and_9 (and_9_out, g, C);
  and and_10 (and_10_out, and_6_out, C);
  or or_1 (a, and_1_out, g);
  or or_2 (b, not_3_out, not_1_out);
  or or_3 (or_3_out, and_2_out, and_3_out);
  or or_4 (d, and_5_out, g);
  or or_5 (f, and_8_out, and_9_out);
  or or_6 (c_2, or_3_out, and_4_out);
  or or_7 (e, and_10_out, and_7_out);

  // Notes on the sheet:
  //   CSE 231L Sec: 8
  //   Group Number: 6
  //   B
  //   A
  //   A NOT
  //   F=B'+C+A
  //   F=B'+C+A
  //   F=D+C'A'+CA+C'B
  //   F=BA+B'A'+C'
  //   F=C'A'+CB'A+C'B+BA'
  //   F=BA+B'A'+C'
  //   F=C'A'+CB'A+C'B+BA'
endmodule
