// Logisim project Project_Flip_Flop.circ as structural Verilog: 1 circuit, main circuit main
module main (
  input  Vcc,
  output a,
  output b,
  output c,
  output d,
  output e,
  output f,
  output g
);

  wire and_1_out, and_2_out, and_3_out, and_4_out, and_5_out, and_6_out, and_7_out, and_8_out, and_9_out,
       and_10_out, and_11_out, clock_1_out, j_k_ff_1_q, j_k_ff_1_qn, j_k_ff_2_q, j_k_ff_3_q, j_k_ff_3_qn,
       or_3_out;

  Clock clock_1 (.out(clock_1_out));
  _7_Segment_Display u_7_segment_display_1 (.g(g), .f(f), .a(a), .b(b), .e(e), .d(d), .c(c));  // open: dp
  and and_1 (and_1_out, j_k_ff_2_q, j_k_ff_3_q);
  J_K_Flip_Flop j_k_ff_1 (
    .J(and_1_out), .K(and_1_out), .clk(clock_1_out), .Q(j_k_ff_1_q), .Qn(j_k_ff_1_qn));  // open: preset, reset
  J_K_Flip_Flop j_k_ff_2 (
    .J(j_k_ff_3_q), .K(j_k_ff_3_q), .clk(clock_1_out), .Q(j_k_ff_2_q), .Qn(g));  // open: preset, reset
  and and_2 (and_2_out, j_k_ff_3_qn, j_k_ff_1_q);
  and and_3 (and_3_out, j_k_ff_1_qn, j_k_ff_2_q);
  and and_4 (and_4_out, j_k_ff_1_q, j_k_ff_3_qn);
  and and_5 (and_5_out, j_k_ff_1_q, g);
  and and_6 (and_6_out, j_k_ff_3_qn, j_k_ff_1_q);
  and and_7 (and_7_out, j_k_ff_3_qn, j_k_ff_2_q);
  and and_8 (and_8_out, j_k_ff_1_qn, g);
  and and_9 (and_9_out, j_k_ff_3_qn, j_k_ff_1_q);
  and and_10 (and_10_out, g, j_k_ff_1_q);
  J_K_Flip_Flop j_k_ff_3 (
    .J(Vcc), .K(Vcc), .clk(clock_1_out), .Q(j_k_ff_3_q), .Qn(j_k_ff_3_qn));  // open: preset, reset
  and and_11 (and_11_out, and_7_out, j_k_ff_1_q);
  or or_1 (a, and_2_out, g);
  or or_2 (b, j_k_ff_3_qn, j_k_ff_1_qn);
  or or_3 (or_3_out, and_3_out, and_4_out);
  or or_4 (d, and_6_out, g);
  or or_5 (f, and_9_out, and_10_out);
  or or_6 (c, or_3_out, and_5_out);
  or or_7 (e, and_11_out, and_8_out);

  // Notes on the sheet:
  //   CSE 231L Sec: 8
  //   Group Number: 6
  //   A
  //   B
  //   C
  //   F=A.C'+A.B'
  //   F=B'+A.C'
  //   F=A'+C'
  //   F=A'.B+A.C'+A.B'
  //   F=B'+A.C'
  //   F=A'.B'+A.B.C'
  //   F=B'
endmodule
